// Logisim project smips.circ as structural Verilog: 10 circuits, main circuit Board
module Board (
);

  wire CLK, HALT, MEM_WE, RESET, TTY_WE;
  wire [3:0] MEM_BE;
  wire [6:0] TTY_DATA;
  wire [31:0] MEM_ADDR, MEM_RDATA, MEM_WDATA;

  Clock Reloj (.out(CLK));
  Button u_Reset (.out(RESET));
  CPU cpu_1 (
    .CLK(CLK), .RESET(RESET), .MEM_RDATA(MEM_RDATA), .MEM_ADDR(MEM_ADDR), .MEM_WDATA(MEM_WDATA),
    .MEM_BE(MEM_BE), .MEM_WE(MEM_WE), .TTY_DATA(TTY_DATA), .TTY_WE(TTY_WE), .HALT(HALT));
  TTY #(.cols(48), .rows(12)) tty_1 (.data(TTY_DATA), .clk(CLK), .we(TTY_WE), .clr(RESET));
  Memory memory_1 (.CLK(CLK), .ADDR(MEM_ADDR), .WDATA(MEM_WDATA), .BE(MEM_BE), .WE(MEM_WE), .RDATA(MEM_RDATA));
  LED u_Halt (.in(HALT));

  // Notes on the sheet:
  //   S-MIPS | Board
  //   No modificar: la CPU se implementa dentro del subcircuito CPU.
endmodule

module CPU (
  input  CLK,
  input  RESET,
  input  [31:0] MEM_RDATA,
  output [31:0] MEM_ADDR,
  output [31:0] MEM_WDATA,
  output [3:0] MEM_BE,
  output MEM_WE,
  output [6:0] TTY_DATA,
  output TTY_WE,
  output HALT
);

  wire beq, bne, fsm_1_out_13, fsm_1_out_14, fsm_1_out_15, fsm_1_out_16, fsm_1_out_17, fsm_1_out_18,
       fsm_1_out_19, fsm_1_out_20, fsm_1_out_21, fsm_1_out_22, fsm_1_out_23, fsm_1_out_25, fsm_1_out_26,
       instruction_decoder_1_out_3, instruction_decoder_1_out_4, instruction_decoder_1_out_5,
       instruction_decoder_1_out_6, instruction_decoder_1_out_7, instruction_decoder_1_out_8, IsBR, lb, lbu,
       lw, sb, sw, ZeroF;
  wire [1:0] fsm_1_out_24, fsm_1_out_27, fsm_1_out_28;
  wire [5:0] Funct, Op;

  Instruction_Decoder instruction_decoder_1 (
    .in_1(Op), .in_2(Funct), .out_3(instruction_decoder_1_out_3), .out_4(instruction_decoder_1_out_4),
    .out_5(instruction_decoder_1_out_5), .out_6(instruction_decoder_1_out_6),
    .out_7(instruction_decoder_1_out_7), .out_8(instruction_decoder_1_out_8), .out_9(HALT), .out_10(beq),
    .out_11(bne), .out_12(lw), .out_13(sw), .out_14(lb), .out_15(lbu), .out_16(sb));
  // Probe on MEM_RDATA
  BranchControl branchcontrol_1 (.in_1(beq), .in_2(bne), .in_3(ZeroF), .out_4(IsBR));
  // Probe on MEM_ADDR
  FSM fsm_1 (
    .in_1(CLK), .in_2(RESET), .in_3(instruction_decoder_1_out_3), .in_4(instruction_decoder_1_out_4),
    .in_5(instruction_decoder_1_out_5), .in_6(IsBR), .in_7(beq), .in_8(bne),
    .in_9(instruction_decoder_1_out_6), .in_10(instruction_decoder_1_out_7),
    .in_11(instruction_decoder_1_out_8), .in_12(HALT), .out_13(fsm_1_out_13), .out_14(fsm_1_out_14),
    .out_15(fsm_1_out_15), .out_16(fsm_1_out_16), .out_17(fsm_1_out_17), .out_18(fsm_1_out_18),
    .out_19(fsm_1_out_19), .out_20(fsm_1_out_20), .out_21(fsm_1_out_21), .out_22(fsm_1_out_22),
    .out_23(fsm_1_out_23), .out_24(fsm_1_out_24), .out_25(fsm_1_out_25), .out_26(fsm_1_out_26),
    .out_27(fsm_1_out_27), .out_28(fsm_1_out_28), .out_29(TTY_WE));
  Datapath datapath_1 (
    .in_22(sw), .in_23(lb), .in_24(lbu), .in_25(sb), .in_20(TTY_WE), .in_21(lw), .in_1(CLK), .in_2(RESET),
    .in_3(fsm_1_out_13), .in_4(fsm_1_out_14), .in_5(fsm_1_out_15), .in_6(fsm_1_out_16), .in_7(fsm_1_out_17),
    .in_8(fsm_1_out_18), .in_9(fsm_1_out_19), .in_10(fsm_1_out_20), .in_11(fsm_1_out_21),
    .in_12(fsm_1_out_22), .in_13(fsm_1_out_23), .in_15(fsm_1_out_25), .in_16(fsm_1_out_26),
    .in_14(fsm_1_out_24), .in_17(fsm_1_out_27), .in_18(fsm_1_out_28), .in_19(MEM_RDATA), .out_27(Op),
    .out_28(Funct), .out_29(ZeroF), .out_30(MEM_ADDR), .out_31(MEM_WDATA), .out_32(MEM_WE), .out_33(TTY_DATA));  // open: out_26

  assign MEM_BE = 4'b1111;

  // Other names for the same wires on the sheet: ADDR[31:0] = MEM_ADDR; Illegal = HALT; RDATA[31:0] = MEM_RDATA;
  //   rst = RESET; TTYDATA[6:0] = TTY_DATA; TTYWE = TTY_WE; WDATA[31:0] = MEM_WDATA; WE = MEM_WE

  // Notes on the sheet:
  //   CPU S-MIPS: implementar aqui
  //   No cambiar nombres, anchos ni sentido de los pines: la placa depende de ellos.
endmodule

module Memory (
  input  CLK,
  input  [31:0] ADDR,
  input  [31:0] WDATA,
  input  [3:0] BE,
  input  WE,
  output [31:0] RDATA
);

  RAM #(.addrWidth(12), .asyncread("true"), .dataWidth(32)) ram_1 (
    .addr(ADDR[13:2]), .we(WE), .oe(1'b1), .clk(CLK), .din(WDATA), .dout(RDATA));
  // Probe on RDATA

  // Other names for the same wires on the sheet: A[11:0] = ADDR[13:2]

  // Notes on the sheet:
  //   Memoria unificada: 4096 palabras de 32 bits (16 KiB), little-endian
  //   Lectura combinacional; escritura en el flanco de subida de CLK con WE=1, solo en los bytes con BE=1.
  //   Se usan los bits 13..2 de ADDR; los demas se ignoran (el espacio se repite cada 16 KiB).
endmodule

module BranchControl (
  input  in_1,
  input  in_2,
  input  in_3,
  output out_4
);

  wire and_1_out, and_2_out, not_1_out;

  and and_1 (and_1_out, in_1, in_3);
  and and_2 (and_2_out, in_2, not_1_out);
  not not_1 (not_1_out, in_3);
  or or_1 (out_4, and_1_out, and_2_out);

  // Other names for the same wires on the sheet: beq = in_1; bne = in_2; brtaken = out_4; ZeroF = in_3

  // Notes on the sheet:
  //   INPUTS
  //   OUTPUTS
  //   Combinational Logic
endmodule

module FSM (
  input  in_1,
  input  in_2,
  input  in_3,
  input  in_4,
  input  in_5,
  input  in_6,
  input  in_7,
  input  in_8,
  input  in_9,
  input  in_10,
  input  in_11,
  input  in_12,
  output out_13,
  output out_14,
  output out_15,
  output out_16,
  output out_17,
  output out_18,
  output out_19,
  output out_20,
  output out_21,
  output out_22,
  output out_23,
  output [1:0] out_24,
  output out_25,
  output out_26,
  output [1:0] out_27,
  output [1:0] out_28,
  output out_29
);

  wire and_2_out, and_3_out, and_4_out, and_5_out, and_6_out, and_7_out, and_8_out, and_9_out, and_10_out,
       and_11_out, and_12_out, and_13_out, and_14_out, and_15_out, D0, D1, D2, D3, not_1_out, or_10_out,
       or_11_out, or_12_out, S1, S2, S9, S10, S11, S12, S13, S15;
  wire [3:0] Qstate;

  Decoder_part #(.select(4)) decoder_1 (
    .out0(out_14), .out1(S1), .out2(S2), .out3(out_19), .out4(out_22), .out5(out_25), .out6(out_27[1]),
    .out7(out_21), .out8(out_26), .out9(S9), .out10(S10), .out11(S11), .out12(S12), .out13(S13),
    .out14(out_29), .out15(S15), .sel(Qstate));  // open: en
  or or_1 (out_18, out_14, S2, S12, out_26, S10);
  or or_2 (out_23, out_27[1], S12);
  or or_3 (out_24[0], out_14, S12, S1);
  not not_1 (not_1_out, in_12);
  Register #(.width(4)) register_1 (.D({D3, D2, D1, D0}), .clk(in_1), .Q(Qstate), .clr(in_2));  // open: en
  or or_4 (out_13, out_14, S13, S9);
  or or_5 (out_24[1], S1, S2, S10, S12);
  and and_1 (out_16, S1, not_1_out);
  // Probe on Qstate
  or or_6 (out_15, out_22, S11, out_21);
  or or_7 (out_20, out_19, out_22);
  or or_8 (out_28[1], out_14, S9);
  or or_9 (out_28[0], S9, S13);
  or or_10 (or_10_out, in_7, in_9, in_8);
  and and_2 (and_2_out, S1, in_3);
  and and_3 (and_3_out, S2, in_5);
  or or_11 (or_11_out, in_5, in_4);
  and and_4 (and_4_out, S1, in_3);
  and and_5 (and_5_out, S1, in_9);
  and and_6 (and_6_out, S2, in_4);
  and and_7 (and_7_out, S1, or_10_out);
  and and_8 (and_8_out, S1, in_10);
  and and_9 (and_9_out, out_26, in_6);
  and and_10 (and_10_out, or_11_out, S1);
  or or_12 (or_12_out, out_27[1], and_4_out);
  and and_11 (and_11_out, S1, in_10);
  and and_12 (and_12_out, out_26, in_6);
  and and_13 (and_13_out, in_11, S1);
  and and_14 (and_14_out, in_11, S1);
  and and_15 (and_15_out, in_11, S1);
  or or_13 (D0, S12, out_14, S2, out_27[1], and_5_out, S10);
  or or_14 (D3, and_12_out, and_7_out, S10, and_8_out, S12, and_13_out);
  or or_15 (D1, and_10_out, and_6_out, or_12_out, and_11_out, S10, and_15_out);
  or or_16 (D2, out_19, and_9_out, and_2_out, and_3_out, S12, out_27[1], and_14_out);

  assign out_17 = out_16;
  assign out_27[0] = out_26;

  // Other names for the same wires on the sheet: ALUOP[1:0] = {out_27[1], out_26}; PCwrCond = out_26; S8 = out_26;
  //   S6 = out_27[1]; ALUSrcA = out_23; ALUSrcB[1:0] = out_24; ALUwr = out_18; Awr = out_16; Bwr = out_16; CLK = in_1;
  //   Dstate[3:0] = {D3, D2, D1, D0}; Illegal = in_12; IorD = out_20; IsBeq = in_7; IsBne = in_8; IsBranch = in_6;
  //   IsImm = in_10; IsJ = in_9; IsLoad = in_4; IsR = in_3; IsStore = in_5; IsSyscall = in_11; PCSource[1:0] = out_28;
  //   PCwr = out_13; Regwr = out_15; RST = in_2; IRwr = out_14; S0 = out_14; MDRwr = out_19; S3 = out_19;
  //   MemToReg = out_22; S4 = out_22; MemWrite = out_25; S5 = out_25; RegDst = out_21; S7 = out_21; S14 = out_29;
  //   TTYWE = out_29

  // Notes on the sheet:
  //   INPUTS
  //   OUTPUTS
  //   StateReg
  //   OUTPUT LOGIC
  //   NEXT STATE LOGIC
endmodule

module Instruction_Decoder (
  input  [5:0] in_1,
  input  [5:0] in_2,
  output out_3,
  output out_4,
  output out_5,
  output out_6,
  output out_7,
  output out_8,
  output out_9,
  output out_10,
  output out_11,
  output out_12,
  output out_13,
  output out_14,
  output out_15,
  output out_16
);

  wire addi, andi, comparator_8_eq, comparator_17_eq, IsBranch, IsJ, IsJal, IsJr, lui, or_6_out, ori, stli;

  Comparator #(.width(6)) comparator_1 (.a(in_1), .b({6{1'b0}}), .eq(out_3));  // open: gt, lt
  Comparator #(.width(6)) comparator_2 (.a(in_1), .b(6'b000100), .eq(out_10));  // open: gt, lt
  Comparator #(.width(6)) comparator_3 (.a(in_1), .b(6'b000101), .eq(out_11));  // open: gt, lt
  Comparator #(.width(6)) comparator_4 (.a(in_1), .b(6'b100011), .eq(out_12));  // open: gt, lt
  Comparator #(.width(6)) comparator_5 (.a(in_1), .b(6'b101011), .eq(out_13));  // open: gt, lt
  Comparator #(.width(6)) comparator_6 (.a(in_1), .b(6'b000010), .eq(IsJ));  // open: gt, lt
  Comparator #(.width(6)) comparator_7 (.a(in_1), .b(6'b000011), .eq(IsJal));  // open: gt, lt
  Comparator #(.width(6)) comparator_8 (.a(in_2), .b(6'b001000), .eq(comparator_8_eq));  // open: gt, lt
  Comparator #(.width(6)) comparator_9 (.a(in_1), .b(6'b100000), .eq(out_14));  // open: gt, lt
  Comparator #(.width(6)) comparator_10 (.a(in_1), .b(6'b100100), .eq(out_15));  // open: gt, lt
  Comparator #(.width(6)) comparator_11 (.a(in_1), .b(6'b101000), .eq(out_16));  // open: gt, lt
  Comparator #(.width(6)) comparator_12 (.a(in_1), .b(6'b001000), .eq(addi));  // open: gt, lt
  Comparator #(.width(6)) comparator_13 (.a(in_1), .b(6'b001010), .eq(stli));  // open: gt, lt
  Comparator #(.width(6)) comparator_14 (.a(in_1), .b(6'b001100), .eq(andi));  // open: gt, lt
  Comparator #(.width(6)) comparator_15 (.a(in_1), .b(6'b001101), .eq(ori));  // open: gt, lt
  Comparator #(.width(6)) comparator_16 (.a(in_1), .b(6'b001111), .eq(lui));  // open: gt, lt
  and and_1 (IsJr, comparator_8_eq, out_3);
  or or_1 (IsBranch, out_10, out_11);
  Comparator #(.width(6)) comparator_17 (.a(in_2), .b(6'b001100), .eq(comparator_17_eq));  // open: gt, lt
  or or_2 (out_6, IsJ, IsJal, IsJr);
  or or_3 (out_4, out_12, out_14, out_15);
  or or_4 (out_5, out_13, out_16);
  or or_5 (out_7, addi, stli, andi, ori, lui);
  and and_2 (out_8, comparator_17_eq, out_3);
  or or_6 (or_6_out, IsBranch, out_6, out_4, out_3, out_8, out_7, out_5);
  not not_1 (out_9, or_6_out);

  // Other names for the same wires on the sheet: funct[5:0] = in_2; Illegal = out_9; IsBeq = out_10; IsBne = out_11;
  //   IsImm = out_7; IsJump = out_6; IsLB = out_14; IsLBU = out_15; IsLoad = out_4; IsLW = out_12; IsR = out_3;
  //   IsSB = out_16; IsStore = out_5; IsSW = out_13; IsSyscall = out_8; OP[5:0] = in_1

  // Notes on the sheet:
  //   INPUTS
  //   OUTPUTS
  //   Combinatoric Logic
endmodule

module Datapath (
  input  in_1,
  input  in_2,
  input  in_3,
  input  in_4,
  input  in_5,
  input  in_6,
  input  in_7,
  input  in_8,
  input  in_9,
  input  in_10,
  input  in_11,
  input  in_12,
  input  in_13,
  input  [1:0] in_14,
  input  in_15,
  input  in_16,
  input  [1:0] in_17,
  input  [1:0] in_18,
  input  [31:0] in_19,
  input  in_20,
  input  in_21,
  input  in_22,
  input  in_23,
  input  in_24,
  input  in_25,
  output out_26,
  output [5:0] out_27,
  output [5:0] out_28,
  output out_29,
  output [31:0] out_30,
  output [31:0] out_31,
  output out_32,
  output [6:0] out_33
);

  wire and_1_out, EnPC;
  wire [2:0] decoder_1_op;
  wire [4:0] ra, wa;
  wire [7:0] multiplexer_4_out;
  wire [25:6] IR;
  wire [27:0] PC4;
  wire [31:0] A, ALUO, ALUout, BE, BE4, InA, InB, inPC, LoadData, MDR, PC, rd2, signext, wd, zeroext;
  wire [31:7] rd1;
  wire [31:28] Jaddr;

  assign BE = {{16{IR[15]}}, {IR[15:6], out_28}};  // Bit_Extender bit_extender_1
  Shifter #(.width(32)) shifter_1 (.in(BE), .\dist (5'b00010), .out(BE4));
  Adder #(.width(32)) adder_1 (.a(PC), .b(32'h4), .out({Jaddr, PC4}), .cin(1'b0));  // open: cout
  Register #(.width(32)) u_PC (.D(inPC), .en(EnPC), .clk(in_1), .Q(PC), .clr(in_2));
  Register #(.width(32)) u_A (.D({rd1, out_33}), .en(in_6), .clk(in_1), .Q(A), .clr(in_2));
  Multiplexer #(.width(32)) multiplexer_1 (.in0(A), .in1(PC), .out(InA), .sel(in_13));
  Register #(.width(32)) u_MDR (.D(in_19), .en(in_9), .clk(in_1), .Q(MDR), .clr(in_2));
  Decoder decoder_1 (.ALUop(in_17), .FUNCT(out_28), .OP(decoder_1_op));
  Multiplexer #(.width(32)) multiplexer_2 (.in0(PC), .in1(ALUout), .out(out_30), .sel(in_10));
  Multiplexer #(.width(5)) multiplexer_3 (.in0(IR[20:16]), .in1(IR[15:11]), .out(wa), .sel(in_11));
  and and_1 (and_1_out, out_29, in_16);
  Multiplexer #(.select(2), .width(8)) multiplexer_4 (
    .in0(MDR[7:0]), .in1(MDR[15:8]), .in2(MDR[23:16]), .in3(MDR[31:24]), .out(multiplexer_4_out),
    .sel(out_30[1:0]));
  Register #(.width(32)) u_ALUout (.D(ALUO), .en(in_8), .clk(in_1), .Q(ALUout), .clr(in_2));
  Register #(.width(32)) B (.D(rd2), .en(in_7), .clk(in_1), .Q(out_31), .clr(in_2));
  or or_1 (EnPC, and_1_out, in_3);
  assign signext = {{24{multiplexer_4_out[7]}}, multiplexer_4_out};  // Bit_Extender bit_extender_2
  assign zeroext = {{24{1'b0}}, multiplexer_4_out};  // Bit_Extender bit_extender_3
  Register #(.width(32)) u_IR (.D(in_19), .en(in_4), .clk(in_1), .Q({out_27, IR, out_28}), .clr(in_2));
  ALU alu_1 (.in_2(InA), .in_3(InB), .in_4(in_1), .in_1(decoder_1_op), .out_5(ALUO), .ZeroF(out_29));
  Multiplexer #(.select(2), .width(32)) multiplexer_5 (
    .in0(out_31), .in1(32'h4), .in2(BE), .in3(BE4), .out(InB), .sel(in_14));
  Multiplexer #(.width(32)) multiplexer_6 (.in0(ALUout), .in1(LoadData), .out(wd), .sel(in_12));
  Multiplexer #(.select(2), .width(32)) multiplexer_7 (
    .in0(ALUO), .in1(ALUout), .in2({Jaddr, PC4}), .in3({Jaddr, IR, out_28, 2'b00}), .out(inPC), .sel(in_18));
  Multiplexer #(.width(5)) multiplexer_8 (.in0(IR[25:21]), .in1(5'b00100), .out(ra), .sel(in_20));
  Multiplexer #(.select(2), .width(32)) multiplexer_9 (
    .in0(MDR), .in1(signext), .in2(zeroext), .in3({32{1'b0}}), .out(LoadData), .sel({in_24, in_23}));
  // Probe on {rd1, out_33}
  // Probe on wa
  // Probe on ra
  // Probe on wd
  RegFile regfile_1 (
    .in_1(in_1), .in_2(in_2), .in_3(in_5), .in_4(ra), .in_5(IR[20:16]), .in_6(wa), .in_7(wd),
    .OUTPUTS({rd1, out_33}), .out_9(rd2));
  // Probe on ALUO

  assign out_26 = in_20;
  assign out_32 = in_15;

  // Other names for the same wires on the sheet: lb = in_23; lbu = in_24; ADDR[31:0] = out_30; ALUop[1:0] = in_17;
  //   ALUSrcA = in_13; ALUSrcB[1:0] = in_14; ALUwr = in_8; Awr = in_6; B[31:0] = out_31; Bwr = in_7; clk = in_1;
  //   IorD = in_10; IR (some bits) = {out_27, out_28}; OPcode[5:0] = out_27; IRwr = in_4; funct[5:0] = out_28;
  //   Jaddr[27:2] = {IR, out_28}; shamt[4:0] = IR[10:6]; rd[4:0] = IR[15:11]; rt[4:0] = IR[20:16];
  //   rs[4:0] = IR[25:21]; PC4[31:28] = Jaddr; lw = in_21; MDRwr = in_9; MemToReg = in_12; Memwrite = in_15;
  //   PCSource[1:0] = in_18; PCwr = in_3; PCwrCond = in_16; rd1[6:0] = out_33; RDATA[31:0] = in_19; RegDst = in_11;
  //   Regwr = in_5; rst = in_2; sb = in_25; sw = in_22; TTY = in_20; ZeroF = out_29

  // Notes on the sheet:
  //   INPUTS
  //   Splits
  //   Additional Registers
  //   ALU Logic
  //   Mux helpers
  //   Register File
  //   OUTPUTS
endmodule

module ALU (
  input  [2:0] in_1,
  input  [31:0] in_2,
  input  [31:0] in_3,
  input  in_4,
  output [31:0] out_5,
  output ZeroF
);

  wire comparator_1_lt;
  wire [31:0] ADD, AND, COMP_SIGNED, LOGICAL_LEFT, LOGICAL_RIGHT, MINUS, OR;

  // Probe on in_2
  // Probe on in_2
  Adder #(.width(32)) adder_1 (.a(in_2), .b(in_3), .out(ADD));  // open: cin, cout
  Subtractor #(.width(32)) subtractor_1 (.a(in_2), .b(in_3), .out(MINUS));  // open: bin, bout
  Comparator #(.width(32)) comparator_1 (.a(in_2), .b(in_3), .lt(comparator_1_lt));  // open: gt, eq
  Shifter #(.shift("lr"), .width(32)) shifter_1 (.in(in_2), .\dist (in_3[4:0]), .out(LOGICAL_LEFT));
  Shifter #(.shift("lr"), .width(32)) shifter_2 (.in(in_2), .\dist (in_3[4:0]), .out(LOGICAL_RIGHT));
  // Probe on in_3
  // Probe on in_3
  assign AND = in_2 & in_3;  // AND_Gate and_1, 32 bits wide
  assign OR = in_2 | in_3;  // OR_Gate or_1, 32 bits wide
  assign COMP_SIGNED = {{31{comparator_1_lt}}, comparator_1_lt};  // Bit_Extender bit_extender_1
  // Probe on in_1
  // Probe on out_5
  // Probe on out_5
  Multiplexer #(.enable("true"), .select(3), .width(32)) multiplexer_1 (
    .in0(ADD), .in1(MINUS), .in2(AND), .in3(OR), .in4(COMP_SIGNED), .in5(LOGICAL_LEFT), .in6(LOGICAL_RIGHT),
    .in7(in_3), .out(out_5), .sel(in_1));  // open: en
  Comparator #(.width(32)) comparator_2 (.a({32{1'b0}}), .b(out_5), .eq(ZeroF));  // open: gt, lt

  // Other names for the same wires on the sheet: A[31:0] = in_2; B[31:0] = in_3; CLK = in_4; MAIN[31:0] = out_5;
  //   OP[2:0] = in_1; ZERO = ZeroF

  // Notes on the sheet:
  //   000
  //   001
  //   010
  //   011
  //   100
  //   0101
  //   110
  //   INPUTS
  //   OUTPUTS
  //   COMBINATIONAL LOGIC
endmodule

module Decoder (
  input  [1:0] ALUop,
  input  [5:0] FUNCT,
  output [2:0] OP
);

  ROM #(.dataWidth(3)) rom_1 (.addr({FUNCT, ALUop}), .data(OP));

  // Notes on the sheet:
  //   contents of rom_1 (hex, n*v repeats v):
  //   64*0 64*1 5 0 6 31*0 1 0 2 3 4*0 4
endmodule

module RegFile (
  input  in_1,
  input  in_2,
  input  in_3,
  input  [4:0] in_4,
  input  [4:0] in_5,
  input  [4:0] in_6,
  input  [31:0] in_7,
  output [31:0] OUTPUTS,
  output [31:0] out_9
);

  wire decoder_1_out0, decoder_1_out1, decoder_1_out2, decoder_1_out3, decoder_1_out4, decoder_1_out5,
       decoder_1_out6, decoder_1_out7, decoder_1_out8, decoder_1_out9, decoder_1_out10, decoder_1_out11,
       decoder_1_out12, decoder_1_out13, decoder_1_out14, decoder_1_out15, decoder_1_out16, decoder_1_out17,
       decoder_1_out18, decoder_1_out19, decoder_1_out20, decoder_1_out21, decoder_1_out22, decoder_1_out23,
       decoder_1_out24, decoder_1_out25, decoder_1_out26, decoder_1_out27, decoder_1_out28, decoder_1_out29,
       decoder_1_out30, decoder_1_out31, or_1_out, or_2_out, R1, R2, R3, R4, R5, R6, R7, R8, R9, R10, R11,
       R12, R13, R14, R15, R16, R17, R18, R19, R20, R21, R22, R23, R24, R25, R26, R27, R28, R29, R30, R31,
       R32;
  wire [31:0] R1O, R2O, R3O, R4O, R5O, R6O, R7O, R8O, R9O, R10O, R11O, R12O, R13O, R14O, R15O, R16O, R17O,
       R18O, R19O, R20O, R21O, R22O, R23O, R24O, R25O, R26O, R27O, R28O, R29O, R30O, R31O, R32O, wd28, wd29;

  or or_1 (or_1_out, in_3, in_2);
  Multiplexer #(.width(32)) multiplexer_1 (.in0(in_7), .in1(32'h7fff0000), .out(wd29), .sel(or_1_out));
  or or_2 (or_2_out, in_3, in_2);
  Multiplexer #(.width(32)) multiplexer_2 (.in0(in_7), .in1(32'h10008000), .out(wd28), .sel(or_2_out));
  Register #(.width(32)) u_R1 (.D({32{1'b0}}), .clk(in_1), .Q(R1O), .clr(in_2));  // open: en
  Register #(.width(32)) u_R2 (.D(in_7), .en(R2), .clk(in_1), .Q(R2O), .clr(in_2));
  Register #(.width(32)) u_R3 (.D(in_7), .en(R3), .clk(in_1), .Q(R3O), .clr(in_2));
  Register #(.width(32)) u_R4 (.D(in_7), .en(R4), .clk(in_1), .Q(R4O), .clr(in_2));
  Register #(.width(32)) u_R5 (.D(in_7), .en(R5), .clk(in_1), .Q(R5O), .clr(in_2));
  Register #(.width(32)) u_R6 (.D(in_7), .en(R6), .clk(in_1), .Q(R6O), .clr(in_2));
  Register #(.width(32)) u_R7 (.D(in_7), .en(R7), .clk(in_1), .Q(R7O), .clr(in_2));
  Register #(.width(32)) u_R8 (.D(in_7), .en(R8), .clk(in_1), .Q(R8O), .clr(in_2));
  Register #(.width(32)) u_R9 (.D(in_7), .en(R9), .clk(in_1), .Q(R9O), .clr(in_2));
  Register #(.width(32)) u_R10 (.en(R10), .clk(in_1), .Q(R10O), .clr(in_2));  // open: D
  Register #(.width(32)) u_R11 (.D(in_7), .en(R11), .clk(in_1), .Q(R11O), .clr(in_2));
  Register #(.width(32)) u_R12 (.D(in_7), .en(R12), .clk(in_1), .Q(R12O), .clr(in_2));
  Register #(.width(32)) u_R13 (.D(in_7), .en(R13), .clk(in_1), .Q(R13O), .clr(in_2));
  Register #(.width(32)) u_R14 (.D(in_7), .en(R14), .clk(in_1), .Q(R14O), .clr(in_2));
  Register #(.width(32)) u_R15 (.D(in_7), .en(R15), .clk(in_1), .Q(R15O), .clr(in_2));
  Register #(.width(32)) u_R16 (.D(in_7), .en(R16), .clk(in_1), .Q(R16O), .clr(in_2));
  Register #(.width(32)) u_R17 (.D(in_7), .en(R17), .clk(in_1), .Q(R17O), .clr(in_2));
  Register #(.width(32)) u_R18 (.D(in_7), .en(R18), .clk(in_1), .Q(R18O), .clr(in_2));
  Register #(.width(32)) u_R19 (.D(in_7), .en(R19), .clk(in_1), .Q(R19O), .clr(in_2));
  Register #(.width(32)) u_R20 (.D(in_7), .en(R20), .clk(in_1), .Q(R20O), .clr(in_2));
  Register #(.width(32)) u_R21 (.D(in_7), .en(R21), .clk(in_1), .Q(R21O), .clr(in_2));
  Register #(.width(32)) u_R22 (.D(in_7), .en(R22), .clk(in_1), .Q(R22O), .clr(in_2));
  Register #(.width(32)) u_R23 (.D(in_7), .en(R23), .clk(in_1), .Q(R23O), .clr(in_2));
  Register #(.width(32)) u_R24 (.D(in_7), .en(R24), .clk(in_1), .Q(R24O), .clr(in_2));
  Register #(.width(32)) u_R25 (.D(in_7), .en(R25), .clk(in_1), .Q(R25O), .clr(in_2));
  Register #(.width(32)) u_R26 (.D(in_7), .en(R26), .clk(in_1), .Q(R26O), .clr(in_2));
  Register #(.width(32)) u_R27 (.D(in_7), .en(R27), .clk(in_1), .Q(R27O), .clr(in_2));
  Register #(.width(32)) u_R28 (.D(wd28), .en(R28), .clk(in_1), .Q(R28O), .clr(in_2));
  Register #(.width(32)) u_R29 (.D(wd29), .en(R29), .clk(in_1), .Q(R29O), .clr(in_2));
  Register #(.width(32)) u_R30 (.D(in_7), .en(R30), .clk(in_1), .Q(R30O), .clr(in_2));
  Register #(.width(32)) u_R31 (.D(in_7), .en(R31), .clk(in_1), .Q(R31O), .clr(in_2));
  Register #(.width(32)) u_R32 (.D(in_7), .en(R32), .clk(in_1), .Q(R32O), .clr(in_2));
  Decoder_part #(.select(5)) decoder_1 (
    .out0(decoder_1_out0), .out1(decoder_1_out1), .out2(decoder_1_out2), .out3(decoder_1_out3),
    .out4(decoder_1_out4), .out5(decoder_1_out5), .out6(decoder_1_out6), .out7(decoder_1_out7),
    .out8(decoder_1_out8), .out9(decoder_1_out9), .out10(decoder_1_out10), .out11(decoder_1_out11),
    .out12(decoder_1_out12), .out13(decoder_1_out13), .out14(decoder_1_out14), .out15(decoder_1_out15),
    .out16(decoder_1_out16), .out17(decoder_1_out17), .out18(decoder_1_out18), .out19(decoder_1_out19),
    .out20(decoder_1_out20), .out21(decoder_1_out21), .out22(decoder_1_out22), .out23(decoder_1_out23),
    .out24(decoder_1_out24), .out25(decoder_1_out25), .out26(decoder_1_out26), .out27(decoder_1_out27),
    .out28(decoder_1_out28), .out29(decoder_1_out29), .out30(decoder_1_out30), .out31(decoder_1_out31),
    .sel(in_6));  // open: en
  and and_1 (R1, in_3, decoder_1_out0);
  and and_2 (R2, in_3, decoder_1_out1);
  and and_3 (R3, in_3, decoder_1_out2);
  and and_4 (R32, in_3, decoder_1_out31);
  and and_5 (R31, in_3, decoder_1_out30);
  and and_6 (R30, in_3, decoder_1_out29);
  and and_7 (R4, in_3, decoder_1_out3);
  and and_8 (R5, in_3, decoder_1_out4);
  and and_9 (R29, in_3, decoder_1_out28);
  and and_10 (R28, in_3, decoder_1_out27);
  Multiplexer #(.select(5), .width(32)) multiplexer_3 (
    .in0(R1O), .in1(R2O), .in2(R3O), .in3(R4O), .in4(R5O), .in5(R6O), .in6(R7O), .in7(R8O), .in8(R9O),
    .in9(R10O), .in10(R11O), .in11(R12O), .in12(R13O), .in13(R14O), .in14(R15O), .in15(R16O), .in16(R17O),
    .in17(R18O), .in18(R19O), .in19(R20O), .in20(R21O), .in21(R22O), .in22(R23O), .in23(R24O), .in24(R25O),
    .in25(R26O), .in26(R27O), .in27(R28O), .in28(R29O), .in29(R30O), .in30(R31O), .in31(R32O), .out(OUTPUTS),
    .sel(in_4));
  Multiplexer #(.select(5), .width(32)) multiplexer_4 (
    .in0(R1O), .in1(R2O), .in2(R3O), .in3(R4O), .in4(R5O), .in5(R6O), .in6(R7O), .in7(R8O), .in8(R9O),
    .in9(R10O), .in10(R11O), .in11(R12O), .in12(R13O), .in13(R14O), .in14(R15O), .in15(R16O), .in16(R17O),
    .in17(R18O), .in18(R19O), .in19(R20O), .in20(R21O), .in21(R22O), .in22(R23O), .in23(R24O), .in24(R25O),
    .in25(R26O), .in26(R27O), .in27(R28O), .in28(R29O), .in29(R30O), .in30(R31O), .in31(R32O), .out(out_9),
    .sel(in_5));
  and and_11 (R6, in_3, decoder_1_out5);
  and and_12 (R7, in_3, decoder_1_out6);
  and and_13 (R8, in_3, decoder_1_out7);
  and and_14 (R27, in_3, decoder_1_out26);
  and and_15 (R26, in_3, decoder_1_out25);
  and and_16 (R25, in_3, decoder_1_out24);
  and and_17 (R9, in_3, decoder_1_out8);
  and and_18 (R10, in_3, decoder_1_out9);
  and and_19 (R11, in_3, decoder_1_out10);
  and and_20 (R24, in_3, decoder_1_out23);
  and and_21 (R23, in_3, decoder_1_out22);
  and and_22 (R22, in_3, decoder_1_out21);
  and and_23 (R12, in_3, decoder_1_out11);
  and and_24 (R13, in_3, decoder_1_out12);
  and and_25 (R21, in_3, decoder_1_out20);
  and and_26 (R20, in_3, decoder_1_out19);
  and and_27 (R14, in_3, decoder_1_out13);
  and and_28 (R15, in_3, decoder_1_out14);
  and and_29 (R16, in_3, decoder_1_out15);
  and and_30 (R19, in_3, decoder_1_out18);
  and and_31 (R18, in_3, decoder_1_out17);
  and and_32 (R17, in_3, decoder_1_out16);

  // Other names for the same wires on the sheet: CLK = in_1; rd1[31:0] = OUTPUTS; rd2[31:0] = out_9; Regwr = in_3;
  //   rs[4:0] = in_4; RST = in_2; rt[4:0] = in_5; wa_wr[4:0] = in_6; wd[31:0] = in_7

  // Notes on the sheet:
  //   INPUTS
  //   Register Bank
  //   !Utilice 1-index
  //   Register Selector
  //   Output Selector
endmodule
